// Logisim project 32-bit-single-cycle-processor.circ as structural Verilog: 7 circuits, main circuit main
module main (
);

  wire ALU_control_splitter_sub_add_bit, clock_1_out, main_1_zero_flag, main_control_1_alusrc,
       main_control_1_beq, main_control_1_bne, main_control_1_extop, main_control_1_j,
       main_control_1_memread, main_control_1_memtoreg, main_control_1_memwrite, main_control_1_regdst,
       main_control_1_regwrite;
  wire [1:0] ALU_control_splitter_alu_selection, ALU_control_splitter_logical_selector, PC_Control_pcsrc;
  wire [2:0] main_control_1_aluop;
  wire [3:0] ALU_control_alu_control;
  wire [4:0] Inst__Splitter_rd, Inst__Splitter_rs, Inst__Splitter_rt, multiplexer_2_out, RD_Reg_q, RS_Reg_q,
       RT_Reg_q;
  wire [5:0] Func__Reg_q, Inst__Splitter_func, Inst__Splitter_opcode, Opcode_Reg_q;
  wire [15:0] Imm_16_Reg_q, Inst__Splitter_immediate_16;
  wire [25:0] Imm_26_Reg_q, Inst__Splitter_immediate_26;
  wire [29:0] register_1_q;
  wire [31:0] adder_1_out, adder_2_out, Data_memory_dataout, extender__32_bit_output,
       Instruction_Memory_instruction, main_1_alu_out, multiplexer_1_out, multiplexer_3_out,
       multiplexer_4_out, multiplier_1_out, Register_File_read_data_1, Register_File_read_data_2;

  Multiplexer #(.select(2), .width(32), .disabled(0), .enable("false")) multiplexer_1 (
    .in0(adder_1_out), .in1({register_1_q[29:26], Imm_26_Reg_q, 2'b00}), .in2(adder_2_out),
    .out(multiplexer_1_out), .sel(PC_Control_pcsrc));  // open: in3
  Clock clock_1 (.out(clock_1_out));
  Register #(.width(30)) register_1 (
    .D(multiplexer_1_out[31:2]), .en(1'b1), .Q(register_1_q), .clk(clock_1_out), .clr(1'b0));
  _32_bit_single_cycle_processor_instruction_splitter Inst__Splitter (
    .instruction(Instruction_Memory_instruction), .opcode(Inst__Splitter_opcode), .rs(Inst__Splitter_rs),
    .rt(Inst__Splitter_rt), .rd(Inst__Splitter_rd), .func(Inst__Splitter_func),
    .immediate_16(Inst__Splitter_immediate_16), .immediate_26(Inst__Splitter_immediate_26));  // open: shift_amount
  Instruction_Memory Instruction_Memory (.address({register_1_q, 2'b00}), .instruction(Instruction_Memory_instruction));
  Adder #(.width(32)) adder_1 (.a(32'h4), .b({register_1_q, 2'b00}), .out(adder_1_out), .cin(1'b0));  // open: cout
  pc_control PC_Control (
    .jump(main_control_1_j), .bne(main_control_1_bne), .beq(main_control_1_beq), .zero(main_1_zero_flag),
    .PCSrc(PC_Control_pcsrc));
  Register #(.width(26)) Imm_26_Reg (
    .D(Inst__Splitter_immediate_26), .Q(Imm_26_Reg_q), .clk(clock_1_out));  // open: en, clr
  main_control main_control_1 (
    .opcode(Opcode_Reg_q), .RegDst(main_control_1_regdst), .RegWrite(main_control_1_regwrite),
    .ExtOp(main_control_1_extop), .MemRead(main_control_1_memread), .MemWrite(main_control_1_memwrite),
    .MemToReg(main_control_1_memtoreg), .bne(main_control_1_bne), .beq(main_control_1_beq),
    .j(main_control_1_j), .ALUOp(main_control_1_aluop), .ALUSrc(main_control_1_alusrc));
  Register #(.width(16)) Imm_16_Reg (
    .D(Inst__Splitter_immediate_16), .Q(Imm_16_Reg_q), .clk(clock_1_out));  // open: en, clr
  Multiplexer #(.width(5), .disabled(0), .enable("false")) multiplexer_2 (
    .in0(RT_Reg_q), .in1(RD_Reg_q), .out(multiplexer_2_out), .sel(main_control_1_regdst));
  Register #(.width(6)) Func__Reg (.D(Inst__Splitter_func), .Q(Func__Reg_q), .clk(clock_1_out));  // open: en, clr
  _16to32_bit_extender extender (
    ._16_bit_input(Imm_16_Reg_q), .ext_op(main_control_1_extop), ._32_bit_output(extender__32_bit_output));
  alu_control ALU_control (.func(Func__Reg_q), .ALUOp(main_control_1_aluop), .ALU_Control(ALU_control_alu_control));
  Register #(.width(5)) RD_Reg (.D(Inst__Splitter_rd), .Q(RD_Reg_q), .clk(clock_1_out));  // open: en, clr
  _32_Bit_Register_File Register_File (
    .Write_Register(multiplexer_2_out), .Read_Register_1(RS_Reg_q), .Read_Register_2(RT_Reg_q),
    .Write_Data(multiplexer_4_out), .Reg_Write(main_control_1_regwrite), .Clock(clock_1_out),
    .Read_Data_1(Register_File_read_data_1), .Read_Data_2(Register_File_read_data_2));
  Register #(.width(5)) RT_Reg (.D(Inst__Splitter_rt), .Q(RT_Reg_q), .clk(clock_1_out));  // open: en, clr
  Register #(.width(5)) RS_Reg (.D(Inst__Splitter_rs), .Q(RS_Reg_q), .clk(clock_1_out));  // open: en, clr
  Adder #(.width(32)) adder_2 (.a(adder_1_out), .b(multiplier_1_out), .out(adder_2_out), .cin(1'b0));  // open: cout
  Multiplier #(.width(32)) multiplier_1 (
    .a(extender__32_bit_output), .b(32'h4), .out(multiplier_1_out), .cin({32{1'b0}}));  // open: cout
  Multiplexer #(.width(32), .disabled(0), .enable("false")) multiplexer_3 (
    .in0(Register_File_read_data_2), .in1(extender__32_bit_output), .out(multiplexer_3_out),
    .sel(main_control_1_alusrc));
  alu_control_splitter ALU_control_splitter (
    .alu_control(ALU_control_alu_control), .sub_add_bit(ALU_control_splitter_sub_add_bit),
    .alu_selection(ALU_control_splitter_alu_selection),
    .logical_selector(ALU_control_splitter_logical_selector));
  Register #(.width(6)) Opcode_Reg (.D(Inst__Splitter_opcode), .Q(Opcode_Reg_q), .clk(clock_1_out));  // open: en, clr
  design_main main_1 (
    .shift_operation_selector(2'b11), .A(Register_File_read_data_1), .B(multiplexer_3_out),
    .alu_selection(ALU_control_splitter_alu_selection),
    .logical_operation_selector(ALU_control_splitter_logical_selector),
    .sub_add_bit(ALU_control_splitter_sub_add_bit), .alu_out(main_1_alu_out), .zero_flag(main_1_zero_flag));  // open: carry_out, overflow_flag
  _4GB_byte_addressable_memory Data_memory (
    .read(main_control_1_memread), .datain(Register_File_read_data_2), .address(main_1_alu_out),
    .byte_half_word(2'b10), .dataout(Data_memory_dataout), .clock(clock_1_out),
    .write(main_control_1_memwrite));
  Multiplexer #(.width(32), .disabled(0), .enable("false")) multiplexer_4 (
    .in0(main_1_alu_out), .in1(Data_memory_dataout), .out(multiplexer_4_out), .sel(main_control_1_memtoreg));
endmodule

module alu_control (
  input  [5:0] func,
  input  [2:0] ALUOp,
  output [3:0] ALU_Control
);

  wire [3:0] bit_extender_1_out, multiplexer_1_out;

  Multiplexer #(.select(4), .width(4)) multiplexer_1 (
    .in0(4'b0100), .in2(4'b0101), .in4(4'b0001), .in5(4'b0010), .in6(4'b0011), .in10(4'b0110),
    .out(multiplexer_1_out), .sel(func[3:0]), .en(1'b1));  // open: in1, in3, in7, in8, in9, in11, in12, in13, in14, in15
  assign bit_extender_1_out = {{1{1'b0}}, ALUOp};  // Bit_Extender bit_extender_1
  Multiplexer #(.select(3), .width(4)) multiplexer_2 (
    .in0(multiplexer_1_out), .in1(bit_extender_1_out), .in2(bit_extender_1_out), .in3(bit_extender_1_out),
    .in4(bit_extender_1_out), .in5(bit_extender_1_out), .in6(bit_extender_1_out), .in7(bit_extender_1_out),
    .out(ALU_Control), .sel(ALUOp), .en(1'b1));
endmodule

// main control
module main_control (
  input  [5:0] opcode,
  output RegDst,
  output RegWrite,
  output ExtOp,
  output ALUSrc,
  output [2:0] ALUOp,
  output MemRead,
  output MemWrite,
  output MemToReg,
  output bne,
  output beq,
  output j
);

  wire decoder_1_out8, decoder_1_out10, decoder_1_out12, decoder_1_out13, decoder_1_out14, not_1_out;

  not not_1 (not_1_out, opcode[5]);
  Decoder #(.select(5), .disabled(0)) decoder_1 (
    .out0(RegDst), .out2(j), .out4(beq), .out5(bne), .out8(decoder_1_out8), .out10(decoder_1_out10),
    .out12(decoder_1_out12), .out13(decoder_1_out13), .out14(decoder_1_out14), .sel(opcode[4:0]),
    .en(not_1_out));  // open: out1, out3, out6, out7, out9, out11, out15, out16, out17, out18, out19, out20, out21, out22, out23, out24, out25, out26, out27, out28, out29, out30, out31
  Decoder #(.select(5), .disabled(0)) decoder_2 (
    .out3(MemRead), .out11(MemWrite), .sel(opcode[4:0]), .en(opcode[5]));  // open: out0, out1, out2, out4, out5, out6, out7, out8, out9, out10, out12, out13, out14, out15, out16, out17, out18, out19, out20, out21, out22, out23, out24, out25, out26, out27, out28, out29, out30, out31
  nor nor_1 (RegWrite, j, beq, bne, MemWrite);
  nor nor_2 (ExtOp, decoder_1_out12, decoder_1_out13, decoder_1_out14);
  nor nor_3 (ALUSrc, RegDst, beq, bne);
  or or_1 (ALUOp[0], decoder_1_out12, decoder_1_out14, beq, bne);
  or or_2 (ALUOp[1], decoder_1_out13, decoder_1_out14, decoder_1_out10);
  or or_3 (ALUOp[2], decoder_1_out10, decoder_1_out8, MemWrite, MemRead, beq, bne);

  assign MemToReg = MemRead;
endmodule

module instruction_splitter (
  input  [31:0] instruction,
  output [4:0] shift_amount,
  output [5:0] opcode,
  output [4:0] rs,
  output [4:0] rt,
  output [4:0] rd,
  output [5:0] func,
  output [15:0] immediate_16,
  output [25:0] immediate_26
);


  assign func = instruction[5:0];
  assign immediate_16 = instruction[15:0];
  assign immediate_26 = instruction[25:0];
  assign opcode = instruction[31:26];
  assign rd = instruction[15:11];
  assign rs = instruction[25:21];
  assign rt = instruction[20:16];
  assign shift_amount = instruction[10:6];
endmodule

module alu_control_splitter (
  input  [3:0] alu_control,
  output sub_add_bit,
  output [1:0] alu_selection,
  output [1:0] logical_selector
);

  wire not_1_out, not_2_out;

  not not_1 (not_1_out, alu_control[1]);
  not not_2 (not_2_out, alu_control[2]);
  or or_1 (alu_selection[0], alu_control[1], not_2_out);
  or or_2 (alu_selection[1], not_1_out, not_2_out);
  and and_1 (logical_selector[1], alu_control[1], alu_control[0]);

  assign logical_selector[0] = alu_control[1];
  assign sub_add_bit = alu_control[0];
endmodule

module _16to32_bit_extender (
  input  [15:0] _16_bit_input,
  input  ext_op,
  output [31:0] _32_bit_output
);

  and and_1 (_32_bit_output[31], _16_bit_input[15], ext_op);

  assign _32_bit_output[30:0] = {{15{_32_bit_output[31]}}, _16_bit_input};
endmodule

module pc_control (
  input  jump,
  input  bne,
  input  beq,
  input  zero,
  output [1:0] PCSrc
);

  wire and_1_out, and_2_out, not_1_out;

  not not_1 (not_1_out, zero);
  and and_1 (and_1_out, beq, zero);
  and and_2 (and_2_out, bne, not_1_out);
  or or_1 (PCSrc[1], and_1_out, and_2_out);

  assign PCSrc[0] = jump;
endmodule
