// Logisim project 4GB byte-addressable memory.circ as structural Verilog: 1 circuit, main circuit main
module main (
  input  [23:0] address,
  input  Read_Write,
  input  [1:0] A,
  input  [31:0] datain,
  output [31:0] out_5
);

  wire Byte_out, clock_1_out, Half_out, not_1_out, not_2_out, not_3_out, not_4_out, or_1_out, or_2_out,
       Word_out;

  not not_1 (not_1_out, A[0]);
  and Byte (Byte_out, not_1_out, not_2_out);
  not not_2 (not_2_out, A[1]);
  and Half (Half_out, A[0], not_3_out);
  not not_3 (not_3_out, A[1]);
  not not_4 (not_4_out, A[0]);
  and Word (Word_out, not_4_out, A[1]);
  or or_1 (or_1_out, Byte_out, Half_out, Word_out);
  or or_2 (or_2_out, Half_out, Word_out);
  Clock clock_1 (.out(clock_1_out));
  RAM #(.addrWidth(24), .bus("separate")) ram_1 (
    .addr(address), .din(datain[7:0]), .data(out_5[7:0]), .str(Read_Write), .sel(or_1_out), .clk(clock_1_out));  // open: ld, clr
  RAM #(.addrWidth(24), .bus("separate")) ram_2 (
    .addr(address), .din(datain[15:8]), .data(out_5[15:8]), .str(Read_Write), .sel(or_2_out),
    .clk(clock_1_out));  // open: ld, clr
  RAM #(.addrWidth(24), .bus("separate")) ram_3 (
    .addr(address), .din(datain[23:16]), .data(out_5[23:16]), .str(Read_Write), .sel(Word_out),
    .clk(clock_1_out));  // open: ld, clr
  RAM #(.addrWidth(24), .bus("separate")) ram_4 (
    .addr(address), .din(datain[31:24]), .data(out_5[31:24]), .str(Read_Write), .sel(Word_out),
    .clk(clock_1_out));  // open: ld, clr

  // Notes on the sheet:
  //   Byte 0
  //   Byte 1
  //   Byte 2
  //   Byte 3
endmodule
