// Logisim project design.circ as structural Verilog: 5 circuits, main circuit main
module main (
);

  logical_operations logical_operations_1 ();  // open: A, B, selector, enable, out
endmodule

module logical_operations (
  input  [31:0] A,
  input  [31:0] B,
  input  [1:0] selector,
  input  enable,
  output [31:0] out
);

  wire [31:0] and_1_out, not_1_out, or_1_out, xor_1_out;

  assign and_1_out = A & B;  // AND_Gate and_1, 32 bits wide
  assign or_1_out = A | B;  // OR_Gate or_1, 32 bits wide
  assign xor_1_out = A ^ B;  // XOR_Gate xor_1, 32 bits wide
  assign not_1_out = ~or_1_out;  // NOT_Gate not_1, 32 bits wide
  Multiplexer #(.select(2), .width(32)) multiplexer_1 (
    .in0(and_1_out), .in1(or_1_out), .in2(not_1_out), .in3(xor_1_out), .out(out), .sel(selector), .en(enable));
endmodule

module zero_detector (
  input  [31:0] _32_bit_Input,
  output zero_bit_flag
);

  nor nor_1 (zero_bit_flag, _32_bit_Input[0], _32_bit_Input[1], _32_bit_Input[2], _32_bit_Input[3], _32_bit_Input[4], _32_bit_Input[5], _32_bit_Input[6], _32_bit_Input[7], _32_bit_Input[8], _32_bit_Input[9], _32_bit_Input[10], _32_bit_Input[11], _32_bit_Input[12], _32_bit_Input[13], _32_bit_Input[14], _32_bit_Input[15], _32_bit_Input[17], _32_bit_Input[18], _32_bit_Input[19], _32_bit_Input[20], _32_bit_Input[21], _32_bit_Input[22], _32_bit_Input[23], _32_bit_Input[24], _32_bit_Input[25], _32_bit_Input[26], _32_bit_Input[27], _32_bit_Input[28], _32_bit_Input[29], _32_bit_Input[30], _32_bit_Input[31], _32_bit_Input[16]);
endmodule

module shifter (
  input  [31:0] _32_bit_input,
  input  [1:0] shift_op,
  input  [4:0] shift_amount,
  output [31:0] data_out
);

  wire and_1_out, xor_1_out, xor_2_out, xor_3_out, xor_4_out, xor_5_out;
  wire [2:0] multiplexer_6_out;
  wire [3:0] multiplexer_3_out;
  wire [6:0] multiplexer_4_out;
  wire [14:0] multiplexer_2_out;
  wire [27:0] multiplexer_3_out_2;
  wire [30:0] extender__63_32;
  wire [31:0] extender__31_0, multiplexer_1_out, multiplexer_5_out, multiplexer_7_out;
  wire [31:31] multiplexer_8_out;

  xor xor_1 (xor_1_out, shift_amount[4], and_1_out);
  xor xor_2 (xor_2_out, shift_amount[3], and_1_out);
  xor xor_3 (xor_3_out, shift_amount[2], and_1_out);
  xor xor_4 (xor_4_out, shift_amount[1], and_1_out);
  shifter_extender_63_bit extender (
    ._32_bit_input(_32_bit_input), .shift_op(shift_op), ._31_0(extender__31_0), ._63_32(extender__63_32));
  and and_1 (and_1_out, shift_op[1], shift_op[0]);
  xor xor_5 (xor_5_out, shift_amount[0], and_1_out);
  Multiplexer #(.width(32)) multiplexer_1 (
    .in0(extender__31_0), .in1({extender__63_32[15:0], extender__31_0[31:16]}), .out(multiplexer_1_out),
    .sel(xor_1_out), .en(1'b1));
  Multiplexer #(.width(15)) multiplexer_2 (
    .in0(extender__63_32[14:0]), .in1(extender__63_32[30:16]), .out(multiplexer_2_out), .sel(xor_1_out),
    .en(1'b1));
  Multiplexer #(.width(32)) multiplexer_3 (
    .in0(multiplexer_1_out), .in1({multiplexer_2_out[7:0], multiplexer_1_out[31:8]}),
    .out({multiplexer_3_out_2, multiplexer_3_out}), .sel(xor_2_out), .en(1'b1));
  Multiplexer #(.width(7)) multiplexer_4 (
    .in0(multiplexer_2_out[6:0]), .in1(multiplexer_2_out[14:8]), .out(multiplexer_4_out), .sel(xor_2_out),
    .en(1'b1));
  Multiplexer #(.width(32)) multiplexer_5 (
    .in0({multiplexer_3_out_2, multiplexer_3_out}), .in1({multiplexer_4_out[3:0], multiplexer_3_out_2}),
    .out(multiplexer_5_out), .sel(xor_3_out), .en(1'b1));
  Multiplexer #(.width(3)) multiplexer_6 (
    .in0(multiplexer_4_out[2:0]), .in1(multiplexer_4_out[6:4]), .out(multiplexer_6_out), .sel(xor_3_out),
    .en(1'b1));
  Multiplexer #(.width(32)) multiplexer_7 (
    .in0(multiplexer_5_out), .in1({multiplexer_6_out[1:0], multiplexer_5_out[31:2]}),
    .out(multiplexer_7_out), .sel(xor_4_out), .en(1'b1));
  Multiplexer multiplexer_8 (
    .in0(multiplexer_6_out[0]), .in1(multiplexer_6_out[2]), .out(multiplexer_8_out[31]), .sel(xor_4_out),
    .en(1'b1));
  Multiplexer #(.width(32)) multiplexer_9 (
    .in0(multiplexer_7_out), .in1({multiplexer_8_out[31], multiplexer_7_out[31:1]}), .out(data_out),
    .sel(xor_5_out), .en(1'b1));

  // Notes on the sheet:
  //   [31:0]
  //   [47:32]
  //   [31:0]
  //   [39:32]
  //   [31:0]
  //   [34:32]
  //   [31:0]
  //   [32]
endmodule

module shifter_extender_63_bit (
  input  [31:0] _32_bit_input,
  input  [1:0] shift_op,
  output [31:0] _31_0,
  output [30:0] _63_32
);

  wire [30:0] bit_extender_1_out, bit_extender_2_out;

  assign bit_extender_1_out = {{30{1'b0}}, 1'b0};  // Bit_Extender bit_extender_1
  assign bit_extender_2_out = {{30{_32_bit_input[31]}}, _32_bit_input[31]};  // Bit_Extender bit_extender_2
  Multiplexer #(.select(2), .width(31)) multiplexer_1 (
    .in0(bit_extender_1_out), .in1(bit_extender_2_out), .in2(_32_bit_input[30:0]), .in3(_32_bit_input[31:1]),
    .out(_63_32), .sel(shift_op), .en(1'b1));
  Multiplexer #(.select(2), .width(32)) multiplexer_2 (
    .in0(_32_bit_input), .in1(_32_bit_input), .in2(_32_bit_input),
    .in3({_32_bit_input[0], bit_extender_1_out}), .out(_31_0), .sel(shift_op), .en(1'b1));
endmodule
