// Logisim project pipeline-registers.circ as structural Verilog: 3 circuits, main circuit EX
module EX (
  input  RegWrite,
  input  ExtOp,
  input  ALUSrc,
  input  [2:0] ALUOp,
  input  [5:0] func,
  input  MemRead,
  input  MemWrite,
  input  MemToReg,
  input  bne,
  input  beq,
  input  j,
  input  CLCK,
  output RegWrite_2,
  output ExtOp_2,
  output ALUSrc_2,
  output [2:0] ALUOp_2,
  output [5:0] func_2,
  output MemRead_2,
  output MemWrite_2,
  output MemToReg_2,
  output bne_2,
  output beq_2,
  output j_2
);

  wire not_1_out;

  Register #(.width(1)) register_1 (.D(RegWrite), .en(1'b1), .Q(RegWrite_2), .clk(CLCK), .clr(not_1_out));
  Register #(.width(1)) register_2 (.D(ExtOp), .en(1'b1), .Q(ExtOp_2), .clk(CLCK), .clr(not_1_out));
  Register #(.width(1)) register_3 (.D(ALUSrc), .en(1'b1), .Q(ALUSrc_2), .clk(CLCK), .clr(not_1_out));
  Register #(.width(3)) register_4 (.D(ALUOp), .en(1'b1), .Q(ALUOp_2), .clk(CLCK), .clr(not_1_out));
  Register #(.width(6)) register_5 (.D(func), .en(1'b1), .Q(func_2), .clk(CLCK), .clr(not_1_out));
  Register #(.width(1)) register_6 (.D(MemRead), .en(1'b1), .Q(MemRead_2), .clk(CLCK), .clr(not_1_out));
  Register #(.width(1)) register_7 (.D(MemWrite), .en(1'b1), .Q(MemWrite_2), .clk(CLCK), .clr(not_1_out));
  Register #(.width(1)) register_8 (.D(MemToReg), .en(1'b1), .Q(MemToReg_2), .clk(CLCK), .clr(not_1_out));
  Register #(.width(1)) register_9 (.D(bne), .en(1'b1), .Q(bne_2), .clk(CLCK), .clr(not_1_out));
  Register #(.width(1)) register_10 (.D(beq), .en(1'b1), .Q(beq_2), .clk(CLCK), .clr(not_1_out));
  Register #(.width(1)) register_11 (.D(j), .en(1'b1), .Q(j_2), .clk(CLCK), .clr(not_1_out));
  not not_1 (not_1_out, 1'b1);
endmodule

module MEM (
  input  MemRead,
  input  MemWrite,
  input  MemToReg,
  input  CLCK,
  input  RegWrite,
  output MemRead_2,
  output MemWrite_2,
  output MemToReg_2,
  output RegWrite_2
);

  wire not_1_out;

  not not_1 (not_1_out, 1'b1);
  Register #(.width(1)) register_1 (.D(MemRead), .en(1'b1), .Q(MemRead_2), .clk(CLCK), .clr(not_1_out));
  Register #(.width(1)) register_2 (.D(MemWrite), .en(1'b1), .Q(MemWrite_2), .clk(CLCK), .clr(not_1_out));
  Register #(.width(1)) register_3 (.D(MemToReg), .en(1'b1), .Q(MemToReg_2), .clk(CLCK), .clr(not_1_out));
  Register #(.width(1)) register_4 (.D(RegWrite), .en(1'b1), .Q(RegWrite_2), .clk(CLCK), .clr(not_1_out));
endmodule

module WB (
  input  RegWrite,
  input  CLK,
  output RegWrite_2
);

  wire not_1_out;

  not not_1 (not_1_out, 1'b1);
  Register #(.width(1)) register_1 (.D(RegWrite), .en(1'b1), .Q(RegWrite_2), .clk(CLK), .clr(not_1_out));
endmodule
